# Fritzing sketch robo (saved by Fritzing 0.9.5d)
breadboards: 2

parts:
  esp1 = ESP32 DevKitc V4
  M1 = fc-51 [package=THT]
  M2 = fc-51 [package=THT]
  M3 = fc-51 [package=THT]
  M4 = fc-51 [package=THT]
  M5 = RioRand LM2596
  BAT1 = 12 battery [package=battery]
  HC-SR04_Sensor_1 = HC-SR04 Ultrasonic Distance Sensor
  Part1 = InvenSense MPU6050
  M6 = 1 chan 5v relay module
  Part2 = HX711 Weighing Sensor Module
  Load_Cell1 = Load Cell - Red/white/black/green
  L298N1 = L298N DC motor driver
  J1 = Dagu DGServo 9g header (male) [package=THT]
  M8 = DC Motor  # not connected
  M10 = DC Motor  # not connected
  M11 = DC Motor  # not connected
  M12 = DC Motor  # not connected

nets:
  N1: esp1.IO2, M1.pin1
  N2: esp1.IO4, HC-SR04_Sensor_1.TRIG
  N3: esp1.IO5, HC-SR04_Sensor_1.ECHO
  N4: esp1.IO18, Part2.DO/RX
  N5: esp1.IO19, Part2.CK/TX
  N6: esp1.IO21, Part1.SDA
  N7: esp1.IO22, Part1.SCL
  N8: esp1.IO23, M2.pin1
  3V3: esp1.3V3, Part1.VCC
  N9: esp1.IO32, L298N1.IN1
  N10: esp1.IO33, L298N1.IN2
  N11: esp1.IO26, L298N1.IN3
  N12: esp1.IO27, M6.pin_3
  N13: esp1.IO14, M4.pin1
  N14: esp1.IO12, L298N1.IN4
  N15: esp1.IO13, M3.pin1
  GND: M1.pin2, M2.pin2, M3.pin2, M4.pin2, M5.Pin_4, Part1.GND, M6.pin_2, Part2.GND
  VCC: M1.pin3, M2.pin3, M3.pin3, M4.pin3, M5.Pin_3, M6.pin_1, Part2.VCC, J1.Vcc
  N16: M5.Pin_1, BAT1.-
  N17: M5.Pin_2, BAT1.+
  N18: Part2.E+, Load_Cell1.wire1
  N19: Part2.E-, Load_Cell1.wire2
  N20: Part2.A+, Load_Cell1.wire3
  N21: Part2.A-, Load_Cell1.wire4
  N22: L298N1.ENA, J1.gnd
  N23: L298N1.ENB, J1.pulse

custom parts:
  ESP32 DevKitc V4: ESP32-DevKitC board with ESP32-WROOM-32 module. ESP32-DevKitC V4 is a small-sized ESP32-based development board produced by Espressif. Most of the pins on the ESP module are broken out to the pin headers on the board. The pins D0, D1, D2, D3, CMD and CLK are used internally for communication between ESP32 and SPI flash memory. They are grouped on both sides near the USB connector. Avoid using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
  12 battery: 12V lead acid type battery, like the Husqvarna YTH2448 12V 35AH battery. The pads in pcb are sized to accomidate up to 14ga wire (as these batterys will deliver high currents.)
  1 chan 5v relay module: 1 Channel 5V Relay Module Board Shield with Optocoupler Support High and Low Level Trigger for Arduino.
  Load Cell - Red/white/black/green: A rectangle load cell/weighting pressure Sensor with four wires - Red, white, black, green. Normally corresponding with E+, E-, A+, A- respectively.
  L298N DC motor driver: 2x DC motor driver with 78M05 positive voltage regulator (7..35 V) L298N: max 46 V, 2 A Set 5 V Enable jumper to enable 5 V regultor (needed for the L298N) and +5 V output at screw terminal or supply external +5 V at screw terminal Set ENA and/or ENB to +5 V to enable motor permanently or supply ENA and/or ENB with PWM signal IN1 and IN2 set rotation directory for motor A (OUT1/OUT2) IN2 and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
